# Fritzing sketch Bean_RTC (saved by Fritzing 0.9.2b)
breadboards: 1

parts:
  VCC1 = 4 x AAA Battery Mount
  RTC1 = RTC-8564NB [package="Module(DIP 8P)"]
  パーツ1 = LightBlue Bean
  R1 = Resistor [tolerance=±5% resistance=220 package=THT]
  R2 = Resistor [tolerance=±5% resistance=220 package="2512 [SMD]"]
  LED1 = LED - 5mm [color="Blue (525nm)" package="5 mm [THT]"]

nets:
  GND: VCC1.-, RTC1.GND, パーツ1.GND
  N1: VCC1.+, RTC1.VDD, R1.Pin_1, R2.Pin_1, LED1.anode
  N2: RTC1.INT, LED1.cathode
  N3: RTC1.SDA, パーツ1.AIN_A0, R1.Pin_0
  N4: RTC1.SCL, パーツ1.AIN_A1, R2.Pin_0

custom parts:
  RTC-8564NB: Real Time Clock Module and I2C-BUS interface method. This product is a module of the SON 8-pin DIP package. Supply voltage 1.8-5.5V
